# Fritzing sketch Duschelicht (saved by Fritzing 0.9.3b)
perfboards: 1

parts:
  R1 = Resistor [tolerance=±5% resistance=10k package=THT]
  R2 = Resistor [tolerance=±5% resistance=220 package=THT]
  Q1 = Basic FET P-Channel [package="TO220 [THT]"]
  C1 = Electrolytic Capacitor [capacitance=100µF voltage=50V package="1010 [SMD, electrolytic]"]  # not connected
  J1 = longpad pin header, 16 pins [form="long pad"]
  LED1 = LED - 5mm [color="Red (633nm)" package="5 mm [THT]"]
  R3 = Resistor [tolerance=±5% resistance=10k package=THT]  # not connected
  RHT1 = Humidity and Temperature Sensor RHT03
  J3 = Infrared Proximity Sensor
  Bauteil1 = Arduino Nano (Rev3.0)
  LED3 = RGB LED (6 legs) [package="5 mm [THT]"]
  Power_plug2 = Power plug
  Power_plug1 = Power plug
  LED4 = LED - 5mm [color="White (6500K)" package="5 mm [THT]"]
  J4 = screw terminal, 4 pins
  J5 = screw terminal, 4 pins

nets:
  N1: R1.Pin_0, J1.pin7, LED3.GND#1
  N2: R1.Pin_1, J1.pin12, Bauteil1.D5
  N3: R2.Pin_0, LED1.anode
  N4: Q1.gate, J1.pin10, Bauteil1.D3
  VCC: J1.pin1, J1.pin14, RHT1.Vcc, Bauteil1.3V3
  N5: J1.pin2, J1.pin13, RHT1.Data-signal, Bauteil1.D6
  N6: J1.pin3, RHT1.GND_2
  N7: J1.pin4, J1.pin15, J3.Vout, Bauteil1.5V
  N8: J1.pin5, J3.GND
  N9: J1.pin6, J1.pin11, J3.Vcc, Bauteil1.D4
  N10: J1.pin16, Bauteil1.GND
  N11: LED3.Blue1, J5.pin2
  N12: LED3.Green, J5.pin1
  N13: Power_plug2.GND, J5.pin4
  N14: Power_plug2.VCC, J5.pin3
  N15: Power_plug1.GND, J4.pin2
  N16: Power_plug1.VCC, J4.pin1
  N17: LED4.cathode, J4.pin4
  N18: LED4.anode, J4.pin3
