# Fritzing sketch Einfache Bewegungsmelder-schaltung (saved by Fritzing 0.9.3b)
perfboards: 1

parts:
  Bauteil1 = Arduino Nano (Rev3.0)
  Q1 = Basic FET P-Channel [package="TO220 [THT]"]  # not connected
  R1 = Resistor [tolerance=±5% resistance=220 package=THT]
  J1 = Infrared Proximity Sensor
  LED1 = LED - 3mm [color="Blue (430nm)" package="3 mm [THT]"]
  LED2 = LED - 3mm [color="White (8000K)" package="3 mm [THT]"]
  Power_plug1 = Power plug

nets:
  VIN: Bauteil1.VIN, Power_plug1.GND
  N1: Bauteil1.5V, LED2.cathode
  N2: Bauteil1.A0, J1.Vcc
  N3: R1.Pin_0, LED2.anode
  N4: R1.Pin_1, LED1.anode
  N5: J1.GND, LED1.cathode
