# Fritzing sketch Julian-Auto (saved by Fritzing 0.9.3b)
perfboards: 1

parts:
  Bauteil1 = Arduino Nano (Rev3.0)
  Power_plug2 = Power plug
  J1 = shrouded pin header, 10 pins [form="♂ (shrouded male)"]  # not connected
  J2 = female pin header, 4 pins [form="♀ (female)"]
  LED1 = RGB LED (com. cathode, rgb) [package="5 mm [THT]"]
  J3 = female pin header, 2 pins [form="♀ (female)"]
  J5 = female pin header, 2 pins [form="♀ (female)"]
  R1 = Rotary Potentiometer (Small) [maximum_resistance=100kΩ package=THT]
  Power_plug3 = Power plug
  S1 = Pushbutton [package="[THT]"]
  S2 = Pushbutton [package="[THT]"]
  S3 = Pushbutton [package="[THT]"]
  Q1 = Basic FET P-Channel [package="TO220 [THT]"]
  Q2 = Basic FET P-Channel [package="TO220 [THT]"]
  Q3 = Basic FET P-Channel [package="TO220 [THT]"]

nets:
  VIN: Bauteil1.VIN, Power_plug2.VCC, J5.pin2
  N1: Bauteil1.A7, R1.wiper
  N2: Bauteil1.A6, S3.Pin_3, S3.Pin_4
  N3: Bauteil1.A5, S2.Pin_3, S2.Pin_4
  N4: Bauteil1.A4, S1.Pin_3, S1.Pin_4
  N5: Bauteil1.A3, Q3.gate
  N6: Bauteil1.A2, Q2.gate
  N7: Bauteil1.A1, Q1.gate
  N8: Power_plug2.GND, J5.pin1
  N9: J2.pin1, LED1.red_anode
  N10: J2.pin2, LED1.common_cathode, Q3.drain
  N11: J2.pin3, LED1.green_anode, Q2.drain
  N12: J2.pin4, LED1.blue_anode, Q1.drain
  N13: J3.pin1, Power_plug3.GND
  N14: J3.pin2, Power_plug3.VCC, Q3.source
  N15: R1.leg2, S1.Pin_1, S1.Pin_2, S3.Pin_1, S3.Pin_2
