# Fritzing sketch Schaltplan Final1 (saved by Fritzing 0.9.2b)
circuit board: 8.46667cm x 5.64444cm
breadboards: 1

parts:
  Raspberry_Pi1 = Raspberry Pi 2
  NPN1_12v_durchgang = NPN-Transistor [package="TO92 [THT]"]
  HitzeLampe_230v = Super Flux LED blue [color=Yellow]
  LED_12v = Super Flux LED blue [color=White]
  Fans_5v = DC Motor
  Relay_240v_durchgang = Relay [part_number=FRS1B-S package=THT]
  Netzteil = DC Power [voltage=12V]
  12->5V_Wandler = DC Power [voltage=5]
  NPN1_5v_durchgang = NPN-Transistor [package="TO92 [THT]"]
  RegenPumpe_12v = DC Motor
  Brunnen_12v = DC Motor
  AusgleichsPumpe_12v = DC Motor
  NPN2_12v_durchgang = NPN-Transistor [package="TO92 [THT]"]
  NPN3_12v_durchgang = NPN-Transistor [package="TO92 [THT]"]
  NPN4_12v_durchgang = NPN-Transistor [package="TO92 [THT]"]
  Lux_Sensor_3v3 = VCNL4000 [package=vcnl4000]
  Feucht/Temp_Sensor_3v3 = Humidity Temperature Sensor SHT15
  WasserStand_Sensor2_3v3 = Pushbutton [package="[THT]"]
  WasserStand_Sensor1_3v3 = Pushbutton [package="[THT]"]
  Moisture_Sensor_3v3 = SHT1x Humdity Sensor [package=sht1x]
  NPN2_5v_durchgang = NPN-Transistor [package="TO92 [THT]"]
  WasserVentil_12v = DC Motor
  Q1 = NPN-Transistor [package="TO92 [THT]"]
  WasserStand_Sensor3_3v3 = Pushbutton [package="[THT]"]

nets:
  3V3: Raspberry_Pi1.3v3, Raspberry_Pi1.3V3, Lux_Sensor_3v3.VDD, Feucht/Temp_Sensor_3v3.VCC, WasserStand_Sensor2_3v3.Pin_3, WasserStand_Sensor2_3v3.Pin_4, WasserStand_Sensor1_3v3.Pin_4, Moisture_Sensor_3v3.VDD, WasserStand_Sensor3_3v3.Pin_4
  N1: Raspberry_Pi1.GPIO2, Lux_Sensor_3v3.SDA, Feucht/Temp_Sensor_3v3.SDA
  N2: Raspberry_Pi1.GPIO3, Lux_Sensor_3v3.SCL, Feucht/Temp_Sensor_3v3.SCL
  N3: Raspberry_Pi1.GPIO4, WasserStand_Sensor1_3v3.Pin_2
  GND: Raspberry_Pi1.GND, LED_12v.cathode, Fans_5v.pin_2, Relay_240v_durchgang.COIL1, Netzteil.V-, 12->5V_Wandler.V-, RegenPumpe_12v.pin_2, Brunnen_12v.pin_2, AusgleichsPumpe_12v.pin_2, Lux_Sensor_3v3.GND, Feucht/Temp_Sensor_3v3.GND, Moisture_Sensor_3v3.GND, WasserVentil_12v.pin_2
  N4: Raspberry_Pi1.GPIO17, WasserStand_Sensor2_3v3.Pin_2
  N5: Raspberry_Pi1.GPIO27, Moisture_Sensor_3v3.DATA
  N6: Raspberry_Pi1.GPIO22, WasserStand_Sensor3_3v3.Pin_1, WasserStand_Sensor3_3v3.Pin_2
  N7: Raspberry_Pi1.GPIO8, NPN2_5v_durchgang.B
  N8: Raspberry_Pi1.GPIO25, Q1.B
  N9: Raspberry_Pi1.GPIO24, NPN4_12v_durchgang.B
  N10: Raspberry_Pi1.GPIO23, NPN3_12v_durchgang.B
  N11: Raspberry_Pi1.GPIO18, NPN2_12v_durchgang.B
  N12: Raspberry_Pi1.GPIO15, NPN1_12v_durchgang.B
  N13: Raspberry_Pi1.GPIO14, NPN1_5v_durchgang.B
  N14: Raspberry_Pi1.5V, NPN1_5v_durchgang.C
  N15: NPN1_12v_durchgang.E, LED_12v.anode
  N16: NPN1_12v_durchgang.C, Netzteil.V+, NPN2_12v_durchgang.C, NPN3_12v_durchgang.C, NPN4_12v_durchgang.C, Q1.C
  N17: HitzeLampe_230v.anode, Relay_240v_durchgang.C1
  GND_2: HitzeLampe_230v.cathode
  N18: Fans_5v.pin_1, NPN2_5v_durchgang.E
  240V: Relay_240v_durchgang.A
  N19: Relay_240v_durchgang.COIL2, NPN1_5v_durchgang.E
  N20: 12->5V_Wandler.V+, NPN2_5v_durchgang.C
  N21: RegenPumpe_12v.pin_1, NPN3_12v_durchgang.E
  N22: Brunnen_12v.pin_1, NPN2_12v_durchgang.E
  N23: AusgleichsPumpe_12v.pin_1, NPN4_12v_durchgang.E
  N24: WasserVentil_12v.pin_1, Q1.E
