# Fritzing sketch Schaltplan Final2 (saved by Fritzing 0.9.2b)
circuit board: 9.89648cm x 5.97412cm
circuit board: 15.2705cm x 12.3793cm
circuit board: 4.40978cm x 4.36952cm
circuit board: 10cm x 6cm
circuit board: 8.62766cm x 5.66346cm
breadboards: 1

parts:
  Raspberry_Pi1 = Raspberry Pi 2
  NPN1_12v_durchgang = NPN-Transistor [package="TO92 [THT]"]
  HitzeLampe_230v = Super Flux LED blue [color=Yellow]
  LED_12v = Super Flux LED blue [color=White]
  Fans_12v = DC Motor
  Relay_240v_durchgang = Relay [part_number=FRS1B-S package=THT]
  Netzteil = DC Power [voltage=12V]
  12->5V_Wandler = DC Power [voltage=5]
  NPN1_5v_durchgang = NPN-Transistor [package="TO92 [THT]"]
  Kaltnebel_12v = DC Motor
  Brunnen_12v = DC Motor
  AusgleichsPumpe_12v = DC Motor
  NPN2_12v_durchgang = NPN-Transistor [package="TO92 [THT]"]
  NPN3_12v_durchgang = NPN-Transistor [package="TO92 [THT]"]
  NPN4_12v_durchgang = NPN-Transistor [package="TO92 [THT]"]
  Lux_Sensor_3v3 = VCNL4000 [package=vcnl4000]
  Feucht/Temp_Sensor_3v3 = Humidity Temperature Sensor SHT15
  WasserStand_Sensor2_3v3 = Pushbutton [package="[THT]"]
  WasserStand_Sensor1_3v3 = Pushbutton [package="[THT]"]
  Moisture_Sensor_3v3 = SHT1x Humdity Sensor [package=sht1x]
  NPN2_12v_durchgang_2 = NPN-Transistor [package="TO92 [THT]"]
  RGB-Led_12v = RGB LED (com. cathode, rgb) [package="5 mm [THT]"]
  channel_1_second = shrouded pin header, 12 pins [form="♂ (shrouded male)"]
  RPi2_con_second = shrouded pin header, 20 pins [form="♂ (shrouded male)"]
  WasserStand_Sensor3_3v3 = Pushbutton [package="[THT]"]
  RegenPumpe_12v = DC Motor
  NachfüllPumpe_12v = DC Motor
  RGB-Led_12v_2 = RGB LED (com. cathode, rgb) [package="5 mm [THT]"]
  RGB-Led_12v_3 = RGB LED (com. cathode, rgb) [package="5 mm [THT]"]
  WasserStand_Sensor4_3v3 = Pushbutton [package="[THT]"]
  WasserVentil_12v = DC Motor
  RGB/Light_PWM = Arduino Power Driver Shield
  RGB-Led_12v_4 = RGB LED (com. cathode, rgb) [package="5 mm [THT]"]
  RGB-Led_12v_5 = RGB LED (com. cathode, rgb) [package="5 mm [THT]"]
  channel_2/3/4_main = double row female pin header, 18 pins [form="♀ (female)"]
  channel_5_second = shrouded pin header, 18 pins [form="♂ (shrouded male)"]
  channel_5_main = double row female pin header, 18 pins [form="♀ (female)"]
  channel_1_main = double row female pin header, 12 pins [form="♀ (female)"]
  RPi2_con_main = double row female pin header, 20 pins [form="♀ (female)"]
  NPN4_12v_durchgang1 = NPN-Transistor [package="TO92 [THT]"]
  NPN4_12v_durchgang2 = NPN-Transistor [package="TO92 [THT]"]
  NPN4_12v_durchgang3 = NPN-Transistor [package="TO92 [THT]"]
  channel_2/3/4_second = shrouded pin header, 18 pins [form="♂ (shrouded male)"]
  D1 = Rectifier Diode [part_number=1N4001 package="300 mil [THT]"]

nets (from the schematic view):
  3V3: Raspberry_Pi1.3v3, Raspberry_Pi1.3V3, RPi2_con_second.pin6
  N1: Raspberry_Pi1.GPIO2, RPi2_con_second.pin5
  N2: Raspberry_Pi1.GPIO3, RPi2_con_second.pin4
  N3: Raspberry_Pi1.GPIO4, RPi2_con_second.pin3
  N4: Raspberry_Pi1.GPIO17, RPi2_con_second.pin2
  N5: Raspberry_Pi1.GPIO27, RPi2_con_second.pin1
  N6: Raspberry_Pi1.GPIO22, RPi2_con_second.pin10
  N7: Raspberry_Pi1.GND, RPi2_con_second.pin8
  N8: Raspberry_Pi1.GPIO21, RPi2_con_second.pin11
  N9: Raspberry_Pi1.GPIO20, RPi2_con_second.pin12
  N10: Raspberry_Pi1.GPIO16, RPi2_con_second.pin13
  N11: Raspberry_Pi1.GPIO12, RPi2_con_second.pin14
  N12: Raspberry_Pi1.ID_SC, RPi2_con_second.pin15
  N13: Raspberry_Pi1.GPIO7, RPi2_con_second.pin16
  N14: Raspberry_Pi1.GPIO8, RPi2_con_second.pin17
  N15: Raspberry_Pi1.GPIO25, RPi2_con_second.pin18
  N16: Raspberry_Pi1.GPIO24, RPi2_con_second.pin19
  N17: Raspberry_Pi1.GPIO23, RPi2_con_second.pin20
  N18: Raspberry_Pi1.5V, RPi2_con_second.pin7
  N19: NPN1_12v_durchgang.E, channel_1_main.pin6
  N20: NPN1_12v_durchgang.B, RPi2_con_main.pin2
  N21: NPN1_12v_durchgang.C, Netzteil.V+, NPN2_12v_durchgang.C, NPN3_12v_durchgang.C, NPN4_12v_durchgang.C, NPN2_12v_durchgang_2.C, channel_2/3/4_main.pin11, channel_5_main.pin7, channel_5_main.pin8, NPN4_12v_durchgang1.C, NPN4_12v_durchgang2.C, NPN4_12v_durchgang3.C
  N22: HitzeLampe_230v.cathode, channel_1_second.pin1
  N23: HitzeLampe_230v.anode, channel_1_second.pin3
  N24: LED_12v.cathode, Fans_12v.pin_2, Lux_Sensor_3v3.GND, channel_1_second.pin2
  N25: LED_12v.anode, RGB-Led_12v.common_cathode, channel_1_second.pin7
  N26: Fans_12v.pin_1, channel_1_second.pin8
  240V: Relay_240v_durchgang.A
  N27: Relay_240v_durchgang.COIL1, Netzteil.V-, 12->5V_Wandler.V-, RGB/Light_PWM.GND, channel_2/3/4_main.pin6, channel_5_main.pin12, channel_5_main.pin13, channel_5_main.pin14, channel_1_main.pin11, RPi2_con_main.pin13
  N28: Relay_240v_durchgang.C1, Relay_240v_durchgang.C2, channel_1_main.pin10
  N29: Relay_240v_durchgang.COIL2, NPN1_5v_durchgang.E
  N30: NPN1_5v_durchgang.B, RPi2_con_main.pin1
  N31: NPN1_5v_durchgang.C, RPi2_con_main.pin14
  N32: Kaltnebel_12v.pin_1, channel_2/3/4_second.pin10
  GND: Kaltnebel_12v.pin_2, Brunnen_12v.pin_2, AusgleichsPumpe_12v.pin_2, Feucht/Temp_Sensor_3v3.GND, Moisture_Sensor_3v3.GND, channel_2/3/4_second.pin13
  N33: Brunnen_12v.pin_1, channel_2/3/4_second.pin11
  N34: AusgleichsPumpe_12v.pin_1, channel_2/3/4_second.pin9
  N35: NPN2_12v_durchgang.E, channel_2/3/4_main.pin8
  N36: NPN2_12v_durchgang.B, RPi2_con_main.pin4
  N37: NPN3_12v_durchgang.E, channel_2/3/4_main.pin9
  N38: NPN3_12v_durchgang.B, RPi2_con_main.pin5
  N39: NPN4_12v_durchgang.E, channel_2/3/4_main.pin10
  N40: NPN4_12v_durchgang.B, RPi2_con_main.pin6
  N41: Lux_Sensor_3v3.SDA, channel_1_second.pin10
  N42: Lux_Sensor_3v3.SCL, channel_1_second.pin9
  N43: Lux_Sensor_3v3.VDD, channel_1_second.pin11
  N44: Feucht/Temp_Sensor_3v3.SCL, channel_2/3/4_second.pin15
  N45: Feucht/Temp_Sensor_3v3.SDA, channel_2/3/4_second.pin14
  VCC: Feucht/Temp_Sensor_3v3.VCC, WasserStand_Sensor2_3v3.Pin_4, WasserStand_Sensor1_3v3.Pin_4, Moisture_Sensor_3v3.VDD, channel_2/3/4_second.pin12
  N46: WasserStand_Sensor2_3v3.Pin_2, channel_2/3/4_second.pin17
  N47: WasserStand_Sensor1_3v3.Pin_2, channel_2/3/4_second.pin16
  N48: Moisture_Sensor_3v3.DATA, channel_2/3/4_second.pin18
  N49: NPN2_12v_durchgang_2.E, channel_1_main.pin5
  N50: NPN2_12v_durchgang_2.B, RPi2_con_main.pin3
  N51: RGB-Led_12v.red_anode, channel_1_second.pin6
  N52: RGB-Led_12v.green_anode, channel_1_second.pin4
  N53: RGB-Led_12v.blue_anode, channel_1_second.pin5
  N54: WasserStand_Sensor3_3v3.Pin_2, channel_5_second.pin2
  N55: WasserStand_Sensor3_3v3.Pin_4, channel_5_second.pin3
  N56: RegenPumpe_12v.pin_1, channel_5_second.pin10
  N57: RegenPumpe_12v.pin_2, channel_5_second.pin5
  N58: NachfüllPumpe_12v.pin_1, channel_5_second.pin9
  N59: NachfüllPumpe_12v.pin_2, channel_5_second.pin6
  N60: RGB-Led_12v_2.red_anode, channel_5_second.pin15
  N61: RGB-Led_12v_2.common_cathode, channel_5_second.pin11
  N62: RGB-Led_12v_2.green_anode, channel_5_second.pin13
  N63: RGB-Led_12v_2.blue_anode, channel_5_second.pin14
  N64: RGB-Led_12v_3.red_anode, channel_5_second.pin18
  N65: RGB-Led_12v_3.common_cathode, channel_5_second.pin12
  N66: RGB-Led_12v_3.green_anode, channel_5_second.pin16
  N67: RGB-Led_12v_3.blue_anode, channel_5_second.pin17
  N68: WasserStand_Sensor4_3v3.Pin_2, channel_5_second.pin1
  N69: WasserStand_Sensor4_3v3.Pin_4, channel_5_second.pin4
  N70: WasserVentil_12v.pin_1, channel_5_second.pin8, D1.cathode
  N71: WasserVentil_12v.pin_2, channel_5_second.pin7, D1.anode
  N72: RGB/Light_PWM.A0, channel_2/3/4_main.pin14
  N73: RGB/Light_PWM.A1, channel_2/3/4_main.pin13
  N74: RGB/Light_PWM.A2, channel_2/3/4_main.pin12
  N75: RGB/Light_PWM.AREF, channel_2/3/4_main.pin5, channel_1_main.pin3, RPi2_con_main.pin16
  N76: RGB/Light_PWM.D2, channel_1_main.pin9
  N77: RGB/Light_PWM.D3, channel_1_main.pin8
  N78: RGB/Light_PWM.D4, channel_1_main.pin7
  N79: RGB/Light_PWM.D5, channel_5_main.pin6
  N80: RGB/Light_PWM.D6, channel_5_main.pin5
  N81: RGB/Light_PWM.D7, channel_5_main.pin4
  N82: RGB/Light_PWM.D8, channel_5_main.pin3
  N83: RGB/Light_PWM.D9, channel_5_main.pin2
  N84: RGB/Light_PWM.D10, channel_5_main.pin1
  N85: RGB/Light_PWM.D11, channel_2/3/4_main.pin17
  N86: RGB/Light_PWM.D12, channel_2/3/4_main.pin16
  N87: RGB/Light_PWM.D13, channel_2/3/4_main.pin15
  N88: RGB/Light_PWM.RESET, channel_2/3/4_main.pin4, channel_1_main.pin4, RPi2_con_main.pin17
  N89: RGB/Light_PWM.VIN, channel_2/3/4_main.pin7, channel_5_main.pin15, channel_5_main.pin16, channel_1_main.pin2, RPi2_con_main.pin15
  N90: RGB-Led_12v_4.red_anode, channel_2/3/4_second.pin4
  N91: RGB-Led_12v_4.common_cathode, RGB-Led_12v_5.common_cathode, channel_2/3/4_second.pin8
  N92: RGB-Led_12v_4.green_anode, channel_2/3/4_second.pin2
  N93: RGB-Led_12v_4.blue_anode, channel_2/3/4_second.pin3
  N94: RGB-Led_12v_5.red_anode, channel_2/3/4_second.pin7
  N95: RGB-Led_12v_5.green_anode, channel_2/3/4_second.pin5
  N96: RGB-Led_12v_5.blue_anode, channel_2/3/4_second.pin6
  N97: channel_2/3/4_main.pin1, RPi2_con_main.pin20
  N98: channel_2/3/4_main.pin2, RPi2_con_main.pin19
  N99: channel_2/3/4_main.pin3, RPi2_con_main.pin18
  N100: channel_5_main.pin9, NPN4_12v_durchgang1.E
  N101: channel_5_main.pin10, NPN4_12v_durchgang2.E
  N102: channel_5_main.pin11, NPN4_12v_durchgang3.E
  N103: channel_5_main.pin17, RPi2_con_main.pin11
  N104: channel_5_main.pin18, RPi2_con_main.pin10
  GND_2: channel_1_main.pin12
  N105: RPi2_con_main.pin7, NPN4_12v_durchgang1.B
  N106: RPi2_con_main.pin8, NPN4_12v_durchgang2.B
  N107: RPi2_con_main.pin9, NPN4_12v_durchgang3.B

notes:
  Terrarium Steuerungs Schaltplan in Channels (1, 2/3/4 und 5) geteilt, 1.1
  channel 5 (Terrarium unten)
  channel 1 (Terrarium oben)
  channel 2/3/4 (Terrarium Mitte)
  channel main (verbindung RPi2)
