# Fritzing sketch T-Schaltplan_Neu (saved by Fritzing 0.9.2b)
breadboards: 1

parts:
  Raspberry_Pi1 = Raspberry Pi 2
  RHT1 = Humidity and Temperature Sensor RHT03
  S1 = Pushbutton [package=THT]  # not connected
  Q1 = NPN-Transistor [package="TO92 [THT]"]
  Q2 = NPN-Transistor [package="TO92 [THT]"]
  M1 = DC Motor
  M2 = DC Motor
  Power_plug1 = Power plug
  Power_plug2 = Power plug
  K1 = Relay [part_number=FRS1B-S package=THT]
  K2 = Relay [part_number=FRS1B-S package=THT]
  LED1 = LED - 5mm [color="Red (633nm)" package="5 mm [THT]"]
  LED2 = LED - 5mm [color="Red (633nm)" package="5 mm [THT]"]
  R1 = Photocell (LDR) [package=THT]
  Q3 = NPN-Transistor [package="TO92 [THT]"]
  M3 = DC Motor
  Q4 = NPN-Transistor [package="TO92 [THT]"]
  Q5 = NPN-Transistor [package="TO92 [THT]"]

nets:
  N1: Raspberry_Pi1.GND, Q1.B, R1.pin_0
  N2: Raspberry_Pi1.GPIO21, R1.pin_1
  N3: Raspberry_Pi1.GPIO20, RHT1.Data-signal
  N4: Raspberry_Pi1.GPIO16, RHT1.Vcc
  N5: Raspberry_Pi1.GPIO23, Q2.B
  N6: Raspberry_Pi1.GPIO18, Q3.B
  N7: Raspberry_Pi1.GPIO15, Q4.B
  N8: Raspberry_Pi1.GPIO14, Q5.B
  N9: RHT1.GND_1, RHT1.GND_2
  N10: Q1.E, K2.COIL2
  N11: Q1.C, Q2.C, Power_plug2.GND, LED1.cathode, Q3.C, Q4.C, Q5.C
  N12: Q2.E, K1.COIL2
  N13: M1.pin_2, Q3.E
  N14: M2.pin_2, Q4.E
  N15: Power_plug1.GND, LED2.cathode
  N16: Power_plug1.VCC, K1.A, K2.A
  N17: K1.C1, K1.C2, LED2.anode
  N18: K2.C1, K2.C2
  N19: M3.pin_2, Q5.E
