# Fritzing sketch terrrium.plan (saved by Fritzing 0.9.2b)
breadboards: 1
stripboards: 1

parts:
  Raspberry_Pi1 = Raspberry Pi 2
  RHT1 = Humidity and Temperature Sensor RHT03
  R1 = Photocell (LDR) [package=THT]
  S1 = Pushbutton [package=THT]
  Q3 = NPN-Transistor [package="TO92 [THT]"]
  Q4 = NPN-Transistor [package="TO92 [THT]"]
  Q5 = NPN-Transistor [package="TO92 [THT]"]
  S2 = Pushbutton [package=THT]
  J1 = Basic Servo
  LED2 = LED - 5mm [color="Red (633nm)" package="5 mm [THT]"]
  LED3 = LED - 5mm [color="Red (633nm)" package="5 mm [THT]"]
  J2 = Infrared Proximity Sensor
  K2 = Relay [part_number=FRS1B-S package=THT]
  Q1 = NPN-Transistor [package="TO92 [THT]"]
  Q2 = NPN-Transistor [package="TO92 [THT]"]
  Power_plug1 = Power plug
  K3 = Relay [part_number=FRS1B-S package=THT]
  Power_plug2 = Power plug
  Q6 = NPN-Transistor [package="TO92 [THT]"]
  M1 = DC Motor
  K4 = Relay [part_number=FRS1B-S package=THT]
  Q7 = NPN-Transistor [package="TO92 [THT]"]
  M2 = DC Motor
  J3 = Basic Force Sensing Resistor (FSR) [package=THT]
  K5 = Relay [part_number=FRS1B-S package=THT]
  Q8 = NPN-Transistor [package="TO92 [THT]"]
  Q9 = NPN-Transistor [package="TO92 [THT]"]
  J4 = Piezo Speaker
  S3 = Pushbutton [package=THT]
  S4 = Pushbutton [package=THT]
  S5 = Pushbutton [package=THT]

nets:
  3V3: Raspberry_Pi1.3v3, Raspberry_Pi1.3V3, RHT1.Vcc, R1.pin_0, J2.Vcc, J3.pin_1
  N1: Raspberry_Pi1.GPIO2, R1.pin_1
  N2: Raspberry_Pi1.GPIO4, Q5.B
  GND: Raspberry_Pi1.GND, RHT1.GND_1, RHT1.GND_2, J1.gnd, J2.GND
  N3: Raspberry_Pi1.GPIO17, Q6.B
  N4: Raspberry_Pi1.GPIO27, Q7.B
  N5: Raspberry_Pi1.GPIO22, S3.leg1
  N6: Raspberry_Pi1.GPIO10, Q4.B
  N7: Raspberry_Pi1.GPIO9, Q3.B
  N8: Raspberry_Pi1.GPIO11, Q2.B
  N9: Raspberry_Pi1.GPIO5, J3.pin_0
  N10: Raspberry_Pi1.GPIO6, J2.Vout
  N11: Raspberry_Pi1.GPIO19, Q9.B
  N12: Raspberry_Pi1.GPIO26, S2.leg1
  N13: Raspberry_Pi1.GPIO21, Q8.B
  N14: Raspberry_Pi1.GPIO20, RHT1.Data-signal
  N15: Raspberry_Pi1.GPIO12, S5.leg1
  N16: Raspberry_Pi1.GPIO7, S4.leg1
  N17: Raspberry_Pi1.GPIO23, S1.leg1
  N18: Raspberry_Pi1.GPIO14, Q1.B
  N19: Raspberry_Pi1.5V, S1.leg0, S2.leg0, S3.leg0, S4.leg0, S5.leg0
  N20: Q3.E, Q4.E, Q5.E, K2.COIL1, Q1.E, Q2.E, K3.COIL1, Q6.E, K4.COIL1, Q7.E, Q8.C
  N21: Q3.C, J4.pin2
  N22: Q5.C, K2.COIL2
  N23: J1.vcc, Q2.C
  N24: J1.pulse, LED2.cathode, Power_plug1.VCC, K5.COIL1, J4.pin1
  N25: LED2.anode, Q1.C
  N26: LED3.cathode, M1.pin_2, M2.pin_2, K5.C1, K5.C2
  N27: LED3.anode, K2.C1, K2.C2
  N28: K2.A, K3.A, Power_plug2.VCC, K4.A
  N29: Power_plug1.GND, Q8.E, Q9.E
  N30: K3.C1, K3.C2, M1.pin_1
  N31: K3.COIL2, Q6.C
  N32: Power_plug2.GND, K5.A
  N33: K4.C1, K4.C2, M2.pin_1
  N34: K4.COIL2, Q7.C
  N35: K5.COIL2, Q9.C

notes:
  230v
